// Logisim project xor.circ as structural Verilog: 2 circuits, main circuit main
module main (
  input  In0,
  input  In1,
  input  In2,
  input  In3,
  output Out,
  output PASS
);

  wire and_1_out, and_2_out, and_3_out, and_4_out, and_5_out, and_6_out, and_7_out, and_8_out, clock_1_out,
       not_1_out, not_2_out, not_3_out, not_4_out, xor_1_c, xor_2_out;
  wire [1:0] counter_1_q;

  Clock clock_1 (.out(clock_1_out));
  // Probe on counter_1_q[1]
  // Probe on counter_1_q[0]
  Counter #(.max('h3), .width(2)) counter_1 (
    .Q(counter_1_q), .clk(clock_1_out), .clr(1'b0));  // open: load, D, count, carry
  not not_1 (not_1_out, In0);
  and and_1 (and_1_out, In1, In2, In3);
  not not_2 (not_2_out, In1);
  and and_2 (and_2_out, In0, In2, In3);
  \xor  xor_1 (.a(counter_1_q[1]), .b(counter_1_q[0]), .c(xor_1_c));
  xor xor_2 (xor_2_out, counter_1_q[0], counter_1_q[1]);
  not not_3 (not_3_out, In2);
  and and_3 (and_3_out, In0, In1, In3);
  // Probe on xor_1_c
  // Probe on xor_2_out
  and and_4 (and_4_out, not_1_out, and_1_out);
  and and_5 (and_5_out, not_2_out, and_2_out);
  not not_4 (not_4_out, In3);
  and and_6 (and_6_out, In0, In1, In2);
  and and_7 (and_7_out, not_3_out, and_3_out);
  xnor xnor_1 (PASS, xor_1_c, xor_2_out);
  and and_8 (and_8_out, not_4_out, and_6_out);
  or or_1 (Out, and_4_out, and_5_out, and_7_out, and_8_out);

  // Notes on the sheet:
  //   Made counter for testing by following:
  //   "Get started with Logisim - A Basic Counter | Advanced Computer Organization" 
  //   www.youtube.com/watch?v=I0ohV3kFtBw
  //   and
  //   "Command-line verification" 
  //   www.cburch.com/logisim/docs/2.6.0/en/guide/verify/index.html
endmodule

module \xor  (
  input  a,
  input  b,
  output c
);

  wire transistor_1_out, transistor_3_out, transistor_5_out, transistor_7_out, transistor_10_out,
       transistor_12_out;

  Transistor transistor_1 (.in(1'b1), .out(transistor_1_out), .gate(a));
  Transistor #(.\type ("n")) transistor_2 (.in(1'b0), .out(transistor_1_out), .gate(a));
  Transistor transistor_3 (.in(1'b1), .out(transistor_3_out), .gate(b));
  Transistor #(.\type ("n")) transistor_4 (.in(1'b0), .out(transistor_3_out), .gate(b));
  Transistor transistor_5 (.in(1'b1), .out(transistor_5_out), .gate(transistor_1_out));
  Transistor transistor_6 (.in(transistor_5_out), .out(c), .gate(b));
  Transistor transistor_7 (.in(1'b1), .out(transistor_7_out), .gate(a));
  Transistor transistor_8 (.in(transistor_7_out), .out(c), .gate(transistor_3_out));
  Transistor #(.\type ("n")) transistor_9 (.in(transistor_10_out), .out(c), .gate(a));
  Transistor #(.\type ("n")) transistor_10 (.in(1'b0), .out(transistor_10_out), .gate(b));
  Transistor #(.\type ("n")) transistor_11 (.in(transistor_12_out), .out(c), .gate(transistor_1_out));
  Transistor #(.\type ("n")) transistor_12 (.in(1'b0), .out(transistor_12_out), .gate(transistor_3_out));
endmodule
