// Logisim project q3.circ as structural Verilog: 1 circuit, main circuit main
module main (
  input  [3:0] A,
  input  [3:0] B,
  output Q
);

  wire and_1_out, and_2_out, and_3_out, and_4_out, and_5_out, and_6_out, and_7_out, xnor_1_out, xnor_2_out,
       xnor_3_out;

  // Probe on A
  // Probe on B
  and and_1 (and_1_out, A[3], ~B[3]);  // AND_Gate
  xnor xnor_1 (xnor_1_out, A[3], B[3]);
  and and_2 (and_2_out, A[2], ~B[2]);  // AND_Gate
  xnor xnor_2 (xnor_2_out, A[2], B[2]);
  and and_3 (and_3_out, A[1], ~B[1]);  // AND_Gate
  xnor xnor_3 (xnor_3_out, A[1], B[1]);
  and and_4 (and_4_out, A[0], ~B[0]);  // AND_Gate
  and and_5 (and_5_out, xnor_1_out, and_2_out);
  and and_6 (and_6_out, xnor_1_out, xnor_2_out, and_3_out);
  and and_7 (and_7_out, xnor_1_out, xnor_2_out, xnor_3_out, and_4_out);
  or or_1 (Q, and_1_out, and_5_out, and_6_out, and_7_out);

  // Notes on the sheet:
  //   Top to bottom:
  //    A3 = 1 && B3 = 0
  //   OR (A3 == B3) && (A2 = 1 && B2 = 0)
  //   OR (A3 == B3) && (A2 == B2) && (A1 = 1 && B1 = 0)
  //   OR (A3 == B3) && (A2 == B2) && (A1 == B1) && (A0 = 1 && B0 = 0)
  //   = A > B
endmodule
