// Logisim project q4.circ as structural Verilog: 4 circuits, main circuit main
module main (
  input  [3:0] A,
  input  [3:0] B,
  input  [3:0] C,
  input  [3:0] D,
  output NotBCD,
  output SixMult
);

  wire adder_1_cout, adder_2_cout, adder_3_cout, comparator_1_lt, comparator_2_lt, comparator_3_lt,
       comparator_4_lt, comparator_5_eq, mod2_1_out_2, not_1_out, not_2_out;
  wire [3:0] adder_1_out, adder_2_out, adder_3_out, mod3_1_out_2, mod3_2_out_2, mod3_3_out_2, mod3_4_out_2,
       mod3_5_out_2;

  // Probe on A
  // Probe on B
  // Probe on C
  // Probe on D
  mod3 mod3_1 (.in_1(A), .out_2(mod3_1_out_2));
  mod3 mod3_2 (.in_1(B), .out_2(mod3_2_out_2));
  mod3 mod3_3 (.in_1(C), .out_2(mod3_3_out_2));
  mod3 mod3_4 (.in_1(D), .out_2(mod3_4_out_2));
  Comparator #(.mode("unsigned"), .width(4)) comparator_1 (.a(4'b1001), .b(A), .lt(comparator_1_lt));  // open: gt, eq
  Comparator #(.mode("unsigned"), .width(4)) comparator_2 (.a(4'b1001), .b(B), .lt(comparator_2_lt));  // open: gt, eq
  Comparator #(.mode("unsigned"), .width(4)) comparator_3 (.a(4'b1001), .b(C), .lt(comparator_3_lt));  // open: gt, eq
  Comparator #(.mode("unsigned"), .width(4)) comparator_4 (.a(4'b1001), .b(D), .lt(comparator_4_lt));  // open: gt, eq
  Adder #(.width(4)) adder_1 (.a(mod3_1_out_2), .b(mod3_2_out_2), .out(adder_1_out), .cin(1'b0), .cout(adder_1_cout));
  // Probe on adder_1_cout
  Adder #(.width(4)) adder_2 (.a(adder_1_out), .b(mod3_3_out_2), .out(adder_2_out), .cin(1'b0), .cout(adder_2_cout));
  // Probe on adder_2_cout
  or or_1 (NotBCD, comparator_1_lt, comparator_2_lt, comparator_3_lt, comparator_4_lt);
  Adder #(.width(4)) adder_3 (.a(adder_2_out), .b(mod3_4_out_2), .out(adder_3_out), .cin(1'b0), .cout(adder_3_cout));
  // Probe on adder_3_cout
  not not_1 (not_1_out, NotBCD);
  Comparator #(.width(4)) comparator_5 (.a(4'b0000), .b(mod3_5_out_2), .eq(comparator_5_eq));  // open: gt, lt
  mod3 mod3_5 (.in_1(adder_3_out), .out_2(mod3_5_out_2));
  not not_2 (not_2_out, mod2_1_out_2);
  mod2 mod2_1 (.in_1(D), .out_2(mod2_1_out_2));
  and and_1 (SixMult, not_1_out, comparator_5_eq, not_2_out);

  // Notes on the sheet:
  //   mod3 before adding to ensure that the sum <= 15 
  //   (max hardcoded case in mod3 subcircuit)
  //   divisible by 3 if sum of digits is divisible by 3
  //   divisible by 6 if divisible by 2 and 3
endmodule

module divides3 (
  input  [3:0] in_1,
  output out_2
);

  wire decoder_1_out0, decoder_1_out3, decoder_1_out6, decoder_1_out9, decoder_1_out12, decoder_1_out15;

  Decoder #(.select(4)) decoder_1 (
    .out0(decoder_1_out0), .out3(decoder_1_out3), .out6(decoder_1_out6), .out9(decoder_1_out9),
    .out12(decoder_1_out12), .out15(decoder_1_out15), .sel(in_1));  // open: out1, out2, out4, out5, out7, out8, out10, out11, out13, out14, en
  or or_1 (out_2, decoder_1_out0, decoder_1_out3, decoder_1_out6, decoder_1_out9, decoder_1_out12, decoder_1_out15);
endmodule

module mod2 (
  input  [3:0] in_1,
  output out_2
);


  assign out_2 = in_1[0];
endmodule

module mod3 (
  input  [3:0] in_1,
  output [3:0] out_2
);

  Multiplexer #(.enable("false"), .select(4), .width(4)) multiplexer_1 (
    .in0(4'b0000), .in1(4'b0001), .in2(4'b0010), .in3(4'b0000), .in4(4'b0001), .in5(4'b0010), .in6(4'b0000),
    .in7(4'b0001), .in8(4'b0010), .in9(4'b0000), .in10(4'b0001), .in11(4'b0010), .in12(4'b0000),
    .in13(4'b0001), .in14(4'b0010), .in15(4'b0000), .out(out_2), .sel(in_1));
endmodule
