// Logisim project q1.circ as structural Verilog: 1 circuit, main circuit main
module main (
  input  [3:0] in_1,
  input  write,
  input  [7:0] in_3
);

  wire decoder_1_out0, decoder_1_out1, decoder_1_out2, decoder_1_out3, decoder_1_out4, decoder_1_out5,
       decoder_1_out6, decoder_1_out7, decoder_1_out8, decoder_1_out9, decoder_1_out10, decoder_1_out11,
       decoder_1_out12, decoder_1_out13, decoder_1_out14, decoder_1_out15;
  wire [3:0] multiplexer_1_out, multiplexer_1_out_2;
  wire [7:0] register_1_q, register_2_q, register_3_q, register_4_q, register_5_q, register_6_q,
       register_7_q, register_8_q, register_9_q, register_10_q, register_11_q, register_12_q, register_13_q,
       register_14_q, register_15_q, register_16_q;

  Hex_Digit_Display hex_digit_display_1 (.value(in_3[7:4]));  // open: dp
  Hex_Digit_Display hex_digit_display_2 (.value(in_3[3:0]));  // open: dp
  Decoder #(.enable("false"), .select(4)) decoder_1 (
    .out0(decoder_1_out0), .out1(decoder_1_out1), .out2(decoder_1_out2), .out3(decoder_1_out3),
    .out4(decoder_1_out4), .out5(decoder_1_out5), .out6(decoder_1_out6), .out7(decoder_1_out7),
    .out8(decoder_1_out8), .out9(decoder_1_out9), .out10(decoder_1_out10), .out11(decoder_1_out11),
    .out12(decoder_1_out12), .out13(decoder_1_out13), .out14(decoder_1_out14), .out15(decoder_1_out15),
    .sel(in_1));
  Register register_1 (.D(in_3), .en(decoder_1_out0), .Q(register_1_q), .clk(write));  // open: clr
  Register register_2 (.D(in_3), .en(decoder_1_out1), .Q(register_2_q), .clk(write), .clr(1'b0));
  Register register_3 (.D(in_3), .en(decoder_1_out2), .Q(register_3_q), .clk(write), .clr(1'b0));
  Register register_4 (.D(in_3), .en(decoder_1_out3), .Q(register_4_q), .clk(write), .clr(1'b0));
  Register register_5 (.D(in_3), .en(decoder_1_out4), .Q(register_5_q), .clk(write), .clr(1'b0));
  Register register_6 (.D(in_3), .en(decoder_1_out5), .Q(register_6_q), .clk(write), .clr(1'b0));
  Register register_7 (.D(in_3), .en(decoder_1_out6), .Q(register_7_q), .clk(write), .clr(1'b0));
  Register register_8 (.D(in_3), .en(decoder_1_out7), .Q(register_8_q), .clk(write), .clr(1'b0));
  Register register_9 (.D(in_3), .en(decoder_1_out8), .Q(register_9_q), .clk(write), .clr(1'b0));
  Register register_10 (.D(in_3), .en(decoder_1_out9), .Q(register_10_q), .clk(write), .clr(1'b0));
  Register register_11 (.D(in_3), .en(decoder_1_out10), .Q(register_11_q), .clk(write), .clr(1'b0));
  Register register_12 (.D(in_3), .en(decoder_1_out11), .Q(register_12_q), .clk(write), .clr(1'b0));
  Register register_13 (.D(in_3), .en(decoder_1_out12), .Q(register_13_q), .clk(write), .clr(1'b0));
  Register register_14 (.D(in_3), .en(decoder_1_out13), .Q(register_14_q), .clk(write), .clr(1'b0));
  Register register_15 (.D(in_3), .en(decoder_1_out14), .Q(register_15_q), .clk(write), .clr(1'b0));
  Register register_16 (.D(in_3), .en(decoder_1_out15), .Q(register_16_q), .clk(write), .clr(1'b0));
  Multiplexer #(.enable("false"), .select(4), .width(8)) multiplexer_1 (
    .in0(register_1_q), .in1(register_2_q), .in2(register_3_q), .in3(register_4_q), .in4(register_5_q),
    .in5(register_6_q), .in6(register_7_q), .in7(register_8_q), .in8(register_9_q), .in9(register_10_q),
    .in10(register_11_q), .in11(register_12_q), .in12(register_13_q), .in13(register_14_q),
    .in14(register_15_q), .in15(register_16_q), .out({multiplexer_1_out_2, multiplexer_1_out}), .sel(in_1));
  Hex_Digit_Display hex_digit_display_3 (.value(multiplexer_1_out_2));  // open: dp
  Hex_Digit_Display hex_digit_display_4 (.value(multiplexer_1_out));  // open: dp

  // Notes on the sheet:
  //   data in
  //   address
  //   (rising edge)
  //   Partially based on ram.circ  (Lecture Notes: Fun with Flip-Flops)
  //   data out
endmodule
