// Logisim project q2.circ as structural Verilog: 1 circuit, main circuit main
module main (
  input  [3:0] most_significant_nibble_of_8_bit_address,
  input  [3:0] least_significant_nibble_of_8_bit_address,
  input  write__rising_edge,
  input  [7:0] data_in__8_bits,
  output [7:0] data_out__8_bits
);

  wire comparator_1_eq;
  wire [3:0] controlled_buffer_1_out;

  Comparator #(.width(4)) comparator_1 (
    .a(4'b1111), .b(most_significant_nibble_of_8_bit_address), .eq(comparator_1_eq));  // open: gt, lt
  assign controlled_buffer_1_out = comparator_1_eq ? least_significant_nibble_of_8_bit_address : 4'bz;  // Controlled_Buffer controlled_buffer_1
  RAM #(.addrWidth(4)) ram_1 (
    .addr(controlled_buffer_1_out), .we(comparator_1_eq), .clk(write__rising_edge), .din(data_in__8_bits),
    .dout(data_out__8_bits));

  // Notes on the sheet:
  //   arbitrary 4-bit constant "Y"
endmodule
