// Logisim project q1.circ as structural Verilog: 1 circuit, main circuit main
module main (
  input  [2:0] CC,
  input  [3:0] ifun,
  output Q
);

  wire not_1_out, not_2_out, not_3_out, or_1_out, xor_1_out;

  // Probe on ifun
  xor xor_1 (xor_1_out, CC[0], CC[1]);
  or or_1 (or_1_out, CC[2], xor_1_out);
  not not_1 (not_1_out, CC[2]);
  not not_2 (not_2_out, xor_1_out);
  not not_3 (not_3_out, or_1_out);
  Multiplexer #(.enable("false"), .select(4)) multiplexer_1 (
    .in0(1'b1), .in1(or_1_out), .in2(xor_1_out), .in3(CC[2]), .in4(not_1_out), .in5(not_2_out),
    .in6(not_3_out), .in7(1'b0), .in8(1'b0), .in9(1'b0), .in10(1'b0), .in11(1'b0), .in12(1'b0), .in13(1'b0),
    .in14(1'b0), .in15(1'b0), .out(Q), .sel(ifun));

  // Notes on the sheet:
  //   Z S O
  //   jmp  7 0
  //   jle 	7 1
  //   jl 	  7 2
  //   je	  7 3
  //   jne	7 4
  //   jge	7 5
  //   jg 	 7 6
  //   = Cnd(CC, ifun)
endmodule
