// Logisim project alu.circ as structural Verilog: 3 circuits, main circuit alu
module alu (
  input  [31:0] aluA,
  input  [31:0] aluB,
  input  [3:0] aluOP,
  output [2:0] CC,
  output [31:0] valE___aluB_OP_aluA
);

  wire addl_1_o, subl_1_o;
  wire [31:0] addl_1_vale___alub___alua, and_1_out, subl_1_vale___alub___alua, xor_1_out;

  // Probe on aluA
  // Probe on aluB
  addl addl_1 (.aluA(aluA), .aluB(aluB), .valE___aluB___aluA(addl_1_vale___alub___alua), .O(addl_1_o));
  subl subl_1 (.aluA(aluA), .aluB(aluB), .valE___aluB___aluA(subl_1_vale___alub___alua), .O(subl_1_o));
  assign and_1_out = aluA & aluB;  // AND_Gate and_1, 32 bits wide
  assign xor_1_out = aluA ^ aluB;  // XOR_Gate xor_1, 32 bits wide
  Multiplexer #(.enable("false"), .select(4)) multiplexer_1 (
    .in0(addl_1_o), .in1(subl_1_o), .in2(1'b0), .in3(1'b0), .out(CC[0]), .sel(aluOP));  // open: in4, in5, in6, in7, in8, in9, in10, in11, in12, in13, in14, in15
  Multiplexer #(.enable("false"), .select(4), .width(32)) multiplexer_2 (
    .in0(addl_1_vale___alub___alua), .in1(subl_1_vale___alub___alua), .in2(and_1_out), .in3(xor_1_out),
    .out({CC[1], valE___aluB_OP_aluA[30:0]}), .sel(aluOP));  // open: in4, in5, in6, in7, in8, in9, in10, in11, in12, in13, in14, in15
  Comparator #(.width(32)) comparator_1 (
    .a({32{1'b0}}), .b({CC[1], valE___aluB_OP_aluA[30:0]}), .eq(CC[2]));  // open: gt, lt
  // Probe on {CC[1], valE___aluB_OP_aluA[30:0]}

  assign valE___aluB_OP_aluA[31] = CC[1];

  // Notes on the sheet:
  //   0: addl
  //   1: subl
  //   2: andl
  //   3: xorl
  //   [Z,S,O]
endmodule

module addl (
  input  [31:0] aluA,
  input  [31:0] aluB,
  output [31:0] valE___aluB___aluA,
  output O
);

  wire and_1_out, and_2_out;

  // Probe on aluA
  // Probe on aluB
  Adder #(.width(32)) adder_1 (.a(aluA), .b(aluB), .out(valE___aluB___aluA));  // open: cin, cout
  and and_1 (and_1_out, valE___aluB___aluA[31], ~aluA[31], ~aluB[31]);  // AND_Gate
  and and_2 (and_2_out, ~valE___aluB___aluA[31], aluA[31], aluB[31]);  // AND_Gate
  // Probe on valE___aluB___aluA
  or or_1 (O, and_1_out, and_2_out);

  // Notes on the sheet:
  //   overflow if:
  //   A, B >= 0 but A+B < 0 OR 
  //   A, B < 0 but A+B > 0
endmodule

module subl (
  input  [31:0] aluA,
  input  [31:0] aluB,
  output [31:0] valE___aluB___aluA,
  output O
);

  wire and_1_out, and_2_out;

  // Probe on aluA
  // Probe on aluB
  Subtractor #(.width(32)) subtractor_1 (.a(aluB), .b(aluA), .out(valE___aluB___aluA));  // open: bin, bout
  and and_1 (and_1_out, valE___aluB___aluA[31], aluA[31], ~aluB[31]);  // AND_Gate
  and and_2 (and_2_out, ~valE___aluB___aluA[31], ~aluA[31], aluB[31]);  // AND_Gate
  // Probe on valE___aluB___aluA
  or or_1 (O, and_1_out, and_2_out);

  // Notes on the sheet:
  //   **Note: B - A
  //   overflow if:
  //   B >= 0, A < 0 but B - A < 0 OR 
  //   B < 0, A >= 0 but B - A > 0
endmodule
