// Logisim project io.circ as structural Verilog: 2 circuits, main circuit io
module io (
  input  KB_Status,
  input  [6:0] KB_Data,
  input  RAM_Use,
  input  [31:0] in_4,
  input  [7:0] in_5,
  input  RAM_Read,
  input  RAM_Write,
  input  TTY_Ready,
  input  reset,
  output KB_read_enable,
  output KB_Clear,
  output [7:0] Outgoing_Data,
  output [6:0] TTY_Data,
  output TTY_Enable,
  output TTY_Clear
);

  wire and_2_out, comparator_1_eq, comparator_2_eq, comparator_3_eq;
  wire [3:0] controlled_buffer_1_out;

  Comparator #(.width(4)) comparator_1 (.a(4'b0100), .b(in_4[3:0]), .eq(comparator_1_eq));  // open: gt, lt
  Comparator #(.width(28)) comparator_2 (.a(28'hfffe0), .b(in_4[31:4]), .eq(comparator_2_eq));  // open: gt, lt
  Comparator #(.width(4)) comparator_3 (.a(4'b1100), .b(in_4[3:0]), .eq(comparator_3_eq));  // open: gt, lt
  and and_1 (KB_read_enable, comparator_1_eq, comparator_2_eq, RAM_Use, RAM_Read);
  and and_2 (and_2_out, RAM_Use, comparator_2_eq, RAM_Read);
  assign controlled_buffer_1_out = and_2_out ? in_4[3:0] : 4'bz;  // Controlled_Buffer controlled_buffer_1
  and and_3 (TTY_Enable, TTY_Ready, RAM_Use, RAM_Write, comparator_2_eq, comparator_3_eq);
  Multiplexer #(.enable("false"), .select(4), .width(8)) multiplexer_1 (
    .in0({{7{1'b0}}, KB_Status}), .in1({8{1'b0}}), .in2({8{1'b0}}), .in3({8{1'b0}}), .in4({1'b0, KB_Data}),
    .in5({8{1'b0}}), .in6({8{1'b0}}), .in7({8{1'b0}}), .in8({{7{1'b0}}, TTY_Ready}), .in9({8{1'b0}}),
    .in10({8{1'b0}}), .in11({8{1'b0}}), .out(Outgoing_Data), .sel(controlled_buffer_1_out));  // open: in12, in13, in14, in15

  assign KB_Clear = reset;
  assign TTY_Clear = reset;
  assign TTY_Data = in_5[6:0];

  // Notes on the sheet:
  //   RAM Address
  //   Incoming Data
endmodule

module test (
  input  [1:0] which_register,
  input  [1:0] which_byte,
  input  Real_address__or_crazy_one,
  input  Use_RAM__please,
  input  read,
  input  write,
  input  [7:0] in_7,
  input  Is_the_display_ready_for_a_new_char____In_your_final_Y86__this_should_be_a_constant_1
);

  wire clock_out, io_1_kb_clear, io_1_kb_read_enable, io_1_tty_clear, io_1_tty_enable, keyboard_1_avail,
       reset_out;
  wire [6:0] io_1_tty_data, keyboard_1_data;
  wire [7:0] io_1_outgoing_data;
  wire [31:0] adder_1_out, multiplexer_1_out, multiplexer_2_out;

  Multiplexer #(.enable("false"), .select(2), .width(32)) multiplexer_1 (
    .in0(32'hfffe00), .in1(32'hfffe04), .in2(32'hfffe08), .in3(32'hfffe0c), .out(multiplexer_1_out),
    .sel(which_register));
  // Probe on io_1_outgoing_data
  Register register_1 (.D(io_1_outgoing_data), .clk(clock_out));  // open: en, Q, clr
  Adder #(.width(32)) adder_1 (
    .a(multiplexer_1_out), .b({{30{1'b0}}, which_byte}), .out(adder_1_out), .cin(1'b0));  // open: cout
  Multiplexer #(.enable("false"), .width(32)) multiplexer_2 (
    .in0(adder_1_out), .in1(32'hcafe), .out(multiplexer_2_out), .sel(Real_address__or_crazy_one));
  // Probe on multiplexer_2_out
  Button reset (.out(reset_out));
  io io_1 (
    .KB_Status(keyboard_1_avail), .KB_Data(keyboard_1_data), .KB_read_enable(io_1_kb_read_enable),
    .RAM_Use(Use_RAM__please), .KB_Clear(io_1_kb_clear), .Outgoing_Data(io_1_outgoing_data),
    .in_4(multiplexer_2_out), .in_5(in_7), .RAM_Read(read), .RAM_Write(write),
    .TTY_Ready(Is_the_display_ready_for_a_new_char____In_your_final_Y86__this_should_be_a_constant_1),
    .TTY_Data(io_1_tty_data), .TTY_Enable(io_1_tty_enable), .reset(reset_out), .TTY_Clear(io_1_tty_clear));
  Button clock (.out(clock_out));
  TTY tty_1 (.data(io_1_tty_data), .clk(clock_out), .we(io_1_tty_enable), .clr(io_1_tty_clear));
  Keyboard keyboard_1 (
    .clk(clock_out), .re(io_1_kb_read_enable), .clr(io_1_kb_clear), .avail(keyboard_1_avail),
    .data(keyboard_1_data));

  // Notes on the sheet:
  //   KBSR address
  //   KBDR address
  //   DSR address
  //   DDR address
  //   CPU telling "RAM" what to do
  //   (what the CPU, when reading, captures on clock rise)
  //   data: CPU --> "RAM"
  //   data: CPU <-- "RAM" 
  //   ----------------------------------------------------------------------------------
  //   "CPU," for your testing
  //   specific byte address
  //   ----------------------------------------------------------------------------------
  //   memory-mapped I/O
  //   (which appears to the CPU as "RAM")
endmodule
