// Logisim project reg.circ as structural Verilog: 3 circuits, main circuit regwriter
module main (
  input  [31:0] valE,
  input  [31:0] valM,
  input  [2:0] dstE,
  input  reqE,
  input  [2:0] dstM,
  input  reqM,
  input  clock,
  input  [2:0] srcA,
  input  [2:0] srcB,
  input  clr,
  output [31:0] valA,
  output [31:0] valB
);

  wire regreader_1_clr, regreader_1_clr_2, regreader_1_clr_3, regreader_1_clr_4, regreader_1_clr_5,
       regreader_1_clr_6, regreader_1_clr_7, regreader_1_clr_8, regwriter_1_en, regwriter_1_en_2,
       regwriter_1_en_3, regwriter_1_en_4, regwriter_1_en_5, regwriter_1_en_6, regwriter_1_en_7,
       regwriter_1_en_8;
  wire [31:0] register_1_q, register_2_q, register_3_q, register_4_q, register_5_q, register_6_q,
       register_7_q, register_8_q, regwriter_1_d0, regwriter_1_d1, regwriter_1_d2, regwriter_1_d3,
       regwriter_1_d4, regwriter_1_d5, regwriter_1_d6, regwriter_1_d7;

  regwriter regwriter_1 (
    .D4(regwriter_1_d4), .EN_5(regwriter_1_en_5), .D5(regwriter_1_d5), .D0(regwriter_1_d0),
    .EN_6(regwriter_1_en_6), .D6(regwriter_1_d6), .EN_7(regwriter_1_en_7), .D7(regwriter_1_d7),
    .EN(regwriter_1_en), .EN_8(regwriter_1_en_8), .D1(regwriter_1_d1), .EN_2(regwriter_1_en_2),
    .D2(regwriter_1_d2), .EN_3(regwriter_1_en_3), .D3(regwriter_1_d3), .EN_4(regwriter_1_en_4), .reqE(reqE),
    .reqM(reqM), .dstE(dstE), .dstM(dstM), .valE(valE), .valM(valM));
  Register #(.width(32)) register_1 (
    .D(regwriter_1_d0), .en(regwriter_1_en), .Q(register_1_q), .clk(clock), .clr(regreader_1_clr));
  Register #(.width(32)) register_2 (
    .D(regwriter_1_d1), .en(regwriter_1_en_2), .Q(register_2_q), .clk(clock), .clr(regreader_1_clr_2));
  Register #(.width(32)) register_3 (
    .D(regwriter_1_d2), .en(regwriter_1_en_3), .Q(register_3_q), .clk(clock), .clr(regreader_1_clr_3));
  Register #(.width(32)) register_4 (
    .D(regwriter_1_d3), .en(regwriter_1_en_4), .Q(register_4_q), .clk(clock), .clr(regreader_1_clr_4));
  Register #(.width(32)) register_5 (
    .D(regwriter_1_d4), .en(regwriter_1_en_5), .Q(register_5_q), .clk(clock), .clr(regreader_1_clr_5));
  Register #(.width(32)) register_6 (
    .D(regwriter_1_d5), .en(regwriter_1_en_6), .Q(register_6_q), .clk(clock), .clr(regreader_1_clr_6));
  Register #(.width(32)) register_7 (
    .D(regwriter_1_d6), .en(regwriter_1_en_7), .Q(register_7_q), .clk(clock), .clr(regreader_1_clr_7));
  Register #(.width(32)) register_8 (
    .D(regwriter_1_d7), .en(regwriter_1_en_8), .Q(register_8_q), .clk(clock), .clr(regreader_1_clr_8));
  regreader regreader_1 (
    .valA(valA), .valB(valB), .CLR_5(regreader_1_clr_5), .CLR_6(regreader_1_clr_6),
    .CLR_7(regreader_1_clr_7), .CLR_8(regreader_1_clr_8), .CLR(regreader_1_clr), .CLR_2(regreader_1_clr_2),
    .CLR_3(regreader_1_clr_3), .CLR_4(regreader_1_clr_4), .reset(clr), .srcA(srcA), .srcB(srcB),
    .Q_5(register_5_q), .Q_6(register_6_q), .Q_7(register_7_q), .Q_8(register_8_q), .Q(register_1_q),
    .Q_2(register_2_q), .Q_3(register_3_q), .Q_4(register_4_q));

  // Notes on the sheet:
  //   (hex)
  //   (hex)
  //   (binary)
  //   (binary)
  //   D0
  //   en0
  //   D7
  //   en7
  //   R0
  //   R1
  //   R2
  //   R3
  //   R4
  //   R5
  //   R6
  //   R7
  //   (binary)
  //   Q0
  //   clr0
  //   Q7
  //   clr7
  //   (hex)
  //   (hex)
endmodule

module regwriter (
  input  [2:0] dstE,
  input  reqE,
  input  [2:0] dstM,
  input  reqM,
  input  [31:0] valE,
  input  [31:0] valM,
  output [31:0] D0,
  output EN,
  output [31:0] D1,
  output EN_2,
  output [31:0] D2,
  output EN_3,
  output [31:0] D3,
  output EN_4,
  output [31:0] D4,
  output EN_5,
  output [31:0] D5,
  output EN_6,
  output [31:0] D6,
  output EN_7,
  output [31:0] D7,
  output EN_8
);

  wire decoder_1_out0, decoder_1_out1, decoder_1_out2, decoder_1_out3, decoder_1_out4, decoder_1_out5,
       decoder_1_out6, decoder_1_out7, decoder_2_out0, decoder_2_out1, decoder_2_out2, decoder_2_out3,
       decoder_2_out4, decoder_2_out5, decoder_2_out6, decoder_2_out7;

  Decoder #(.select(3)) decoder_1 (
    .out0(decoder_1_out0), .out1(decoder_1_out1), .out2(decoder_1_out2), .out3(decoder_1_out3),
    .out4(decoder_1_out4), .out5(decoder_1_out5), .out6(decoder_1_out6), .out7(decoder_1_out7), .sel(dstE),
    .en(reqE));
  Decoder #(.select(3)) decoder_2 (
    .out0(decoder_2_out0), .out1(decoder_2_out1), .out2(decoder_2_out2), .out3(decoder_2_out3),
    .out4(decoder_2_out4), .out5(decoder_2_out5), .out6(decoder_2_out6), .out7(decoder_2_out7), .sel(dstM),
    .en(reqM));
  Multiplexer #(.enable("false"), .width(32)) multiplexer_1 (.in0(valE), .in1(valM), .out(D0), .sel(decoder_2_out0));
  or or_1 (EN, decoder_1_out0, decoder_2_out0);
  Multiplexer #(.enable("false"), .width(32)) multiplexer_2 (.in0(valE), .in1(valM), .out(D1), .sel(decoder_2_out1));
  or or_2 (EN_2, decoder_1_out1, decoder_2_out1);
  Multiplexer #(.enable("false"), .width(32)) multiplexer_3 (.in0(valE), .in1(valM), .out(D2), .sel(decoder_2_out2));
  or or_3 (EN_3, decoder_1_out2, decoder_2_out2);
  Multiplexer #(.enable("false"), .width(32)) multiplexer_4 (.in0(valE), .in1(valM), .out(D3), .sel(decoder_2_out3));
  or or_4 (EN_4, decoder_1_out3, decoder_2_out3);
  Multiplexer #(.enable("false"), .width(32)) multiplexer_5 (.in0(valE), .in1(valM), .out(D4), .sel(decoder_2_out4));
  or or_5 (EN_5, decoder_1_out4, decoder_2_out4);
  Multiplexer #(.enable("false"), .width(32)) multiplexer_6 (.in0(valE), .in1(valM), .out(D5), .sel(decoder_2_out5));
  or or_6 (EN_6, decoder_1_out5, decoder_2_out5);
  Multiplexer #(.enable("false"), .width(32)) multiplexer_7 (.in0(valE), .in1(valM), .out(D6), .sel(decoder_2_out6));
  or or_7 (EN_7, decoder_1_out6, decoder_2_out6);
  Multiplexer #(.enable("false"), .width(32)) multiplexer_8 (.in0(valE), .in1(valM), .out(D7), .sel(decoder_2_out7));
  or or_8 (EN_8, decoder_1_out7, decoder_2_out7);

  // Notes on the sheet:
  //   if dstE == dstM && reqE == reqM == 1, vallM is written to the register
endmodule

module regreader (
  input  [2:0] srcA,
  input  [2:0] srcB,
  input  [31:0] Q,
  input  [31:0] Q_2,
  input  [31:0] Q_3,
  input  reset,
  input  [31:0] Q_4,
  input  [31:0] Q_5,
  input  [31:0] Q_6,
  input  [31:0] Q_7,
  input  [31:0] Q_8,
  output CLR,
  output [31:0] valA,
  output [31:0] valB,
  output CLR_2,
  output CLR_3,
  output CLR_4,
  output CLR_5,
  output CLR_6,
  output CLR_7,
  output CLR_8
);

  Multiplexer #(.enable("false"), .select(3), .width(32)) multiplexer_1 (
    .in0(Q), .in1(Q_2), .in2(Q_3), .in3(Q_4), .in4(Q_5), .in5(Q_6), .in6(Q_7), .in7(Q_8), .out(valA),
    .sel(srcA));
  Multiplexer #(.enable("false"), .select(3), .width(32)) multiplexer_2 (
    .in0(Q), .in1(Q_2), .in2(Q_3), .in3(Q_4), .in4(Q_5), .in5(Q_6), .in6(Q_7), .in7(Q_8), .out(valB),
    .sel(srcB));

  assign CLR = reset;
  assign CLR_2 = reset;
  assign CLR_3 = reset;
  assign CLR_4 = reset;
  assign CLR_5 = reset;
  assign CLR_6 = reset;
  assign CLR_7 = reset;
  assign CLR_8 = reset;

  // Notes on the sheet:
  //   for reg 0
  //   for reg 7
endmodule
