// Logisim project useq.circ as structural Verilog: 1 circuit, main circuit useq
module useq (
  input  [5:0] CurrentState,
  input  [5:0] valN,
  input  [3:0] icode,
  input  DMemReady,
  input  IMemReady,
  input  [1:0] select,
  output [5:0] NextState
);

  wire [5:0] multiplexer_1_out, multiplexer_2_out;

  Multiplexer #(.enable("false"), .width(6)) multiplexer_1 (
    .in0(CurrentState), .in1(valN), .out(multiplexer_1_out), .sel(DMemReady));
  Multiplexer #(.enable("false"), .width(6)) multiplexer_2 (
    .in0(CurrentState), .in1({2'b11, icode}), .out(multiplexer_2_out), .sel(IMemReady));
  Multiplexer #(.enable("false"), .select(2), .width(6)) multiplexer_3 (
    .in0(CurrentState), .in1(valN), .in2(multiplexer_1_out), .in3(multiplexer_2_out), .out(NextState),
    .sel(select));

  // Notes on the sheet:
  //   00: CurrentState
  //   01: valN
  //   10: DMemReady == 0 ? CurrentState : valN
  //   11: IMemReady == 0 ? CurrentState : 11[icode]
endmodule
