// Logisim project mmu.circ as structural Verilog: 2 circuits, main circuit main
module main (
  input  [15:0] Logical_Address,
  input  V,
  input  W,
  input  R,
  input  [7:0] frame_num,
  input  Privilege,
  input  RAM_USE,
  input  READ,
  input  WRITE,
  output [15:0] PHYSICAL_ADDRESS,
  output [7:0] Page_num,
  output RAM_USE_2,
  output READ_2,
  output WRITE_2,
  output EXCEPTION
);

  wire [7:0] Actual_Pagetable_dout;
  wire [10:8] Actual_Pagetable_dout_2;

  RAM #(.dataWidth(11)) Actual_Pagetable (
    .addr(Logical_Address[15:8]), .dout({Actual_Pagetable_dout_2, Actual_Pagetable_dout}));  // open: we, clk, din
  // MMU mmu_1: pin names not known; wires that end beside it: Privilege, RAM_USE, READ, WRITE, EXCEPTION, V, W, R, RAM_USE_2, READ_2, WRITE_2

  assign Page_num = Logical_Address[15:8];
  assign PHYSICAL_ADDRESS = {frame_num, Logical_Address[7:0]};

  // Notes on the sheet:
  //   (page table entry)
  //   (for testing/demo)
endmodule

module MMU (
  input  Valid,
  input  Unpriv_Write,
  input  Unpriv_Read,
  input  Privilege,
  input  Ram_Use__in,
  input  Read__in,
  input  Write__in,
  output Ram_Use__out,
  output Read__out,
  output Write__out,
  output Exception
);

  wire or_1_out, or_2_out;

  or or_1 (or_1_out, Unpriv_Read, ~Privilege);  // OR_Gate
  or or_2 (or_2_out, Unpriv_Write, ~Privilege);  // OR_Gate
  and and_1 (Read__out, or_1_out, Valid, Ram_Use__in, Read__in);
  and and_2 (Write__out, or_2_out, Valid, Ram_Use__in, Write__in);
  or or_3 (Ram_Use__out, Read__out, Write__out);
  and and_3 (Exception, ~Ram_Use__out, Ram_Use__in);  // AND_Gate

  // Notes on the sheet:
  //   assumes the CPU will never assert ram_use, 
  //   read and write to all be 1 at the same time
endmodule
