// Logisim project uarch.circ as structural Verilog: 7 circuits, main circuit dpath
module dpath (
  input  in_1,
  input  in_2,
  input  in_3,
  input  in_4,
  input  in_5,
  input  in_6,
  input  in_7,
  input  in_8,
  input  in_9,
  input  in_10,
  input  in_11,
  input  in_12,
  input  in_13,
  input  in_14,
  input  in_15,
  input  in_16,
  input  in_17,
  input  in_18,
  input  _0_add,
  input  in_20,
  input  rB____F,
  input  Reset,
  input  in_23,
  input  in_24,
  output out_25
);

  wire and_1_out, and_2_out, and_4_out, cnd_1_p3, comparator_1_eq, comparator_2_eq, comparator_3_gt,
       comparator_4_eq, comparator_5_gt, comparator_6_eq, comparator_6_lt, D_RAMread, D_RAMuse, D_RAMWrite,
       DMemReady, exception, I_RAMread, I_RAMuse, IMemReady, IMemReq, io_1_kb_clear, io_1_kb_read_enable,
       io_1_tty_clear, io_1_tty_enable, kbyte_buddy_1_sel, kbyte_buddy_2_sel, keyboard_1_avail, ldPriv,
       multiplexer_9_out, multiplexer_13_out, newPriv, or_1_out, or_2_out, or_3_out, or_4_out, or_5_out,
       or_6_out, priv, regreader_1_clr, regreader_1_clr_2, regreader_1_clr_3, regreader_1_clr_4,
       regreader_1_clr_5, regreader_1_clr_6, regreader_1_clr_7, regreader_1_clr_8, regwriter_1_en,
       regwriter_1_en_2, regwriter_1_en_3, regwriter_1_en_4, regwriter_1_en_5, regwriter_1_en_6,
       regwriter_1_en_7, regwriter_1_en_8;
  wire [2:0] alu_1_cc, bit_extender_1_out, bit_extender_2_out, bit_extender_3_out, bit_extender_4_out, cc;
  wire [2:2] nextPCsel;
  wire [3:0] adder_2_out, icode, ifun, multiplexer_3_out, multiplexer_6_out, multiplexer_7_out,
       multiplexer_8_out, multiplexer_12_out, rA, rB;
  wire [4:0] fsm_1_output;
  wire [5:0] fsm_1_state;
  wire [6:0] io_1_tty_data, keyboard_1_data;
  wire [7:0] D_Data_from_RAM, D_Data_to_RAM, ishim_1_out_6, ishim_1_out_7, ishim_1_out_8, ishim_1_out_9,
       ishim_1_out_10, ishim_1_out_11;
  wire [9:0] controlled_buffer_1_out, controlled_buffer_2_out, kbyte_buddy_1_ram_addr, kbyte_buddy_2_ram_addr;
  wire [31:0] adder_1_out, alu_1_vale___alub_op_alua, D_RAMAddr, dhsim_1_dataout, eax_q, ebp_q, ebx_q, ecx_q,
       edi_q, edx_q, esi_q, esp_q, isplit_1_d_v, isplit_1_dest, MAR_q, MDR_q, multiplexer_1_out,
       multiplexer_2_out, multiplexer_4_out, multiplexer_5_out, multiplexer_10_out, multiplexer_11_out,
       multiplexer_14_out, multiplexer_15_out, PC_q, regreader_1_vala, regreader_1_valb, regwriter_1_d0,
       regwriter_1_d1, regwriter_1_d2, regwriter_1_d3, regwriter_1_d4, regwriter_1_d5, regwriter_1_d6,
       regwriter_1_d7;

  Register #(.width(32)) PC (.D(multiplexer_4_out), .en(in_13), .Q(PC_q), .clk(out_25), .clr(Reset));
  Clock Clock (.out(out_25));
  // Probe on I_RAMuse
  // Probe on D_RAMAddr
  // Probe on IMemReq
  // Probe on {in_5, in_6}
  // Probe on multiplexer_1_out
  Multiplexer #(.enable("false"), .select(2), .width(32)) multiplexer_1 (
    .in0(32'h6), .in1(32'h5), .in2(32'h2), .in3(32'h1), .out(multiplexer_1_out), .sel({in_5, in_6}));
  // Probe on I_RAMread
  // Probe on in_20
  Adder #(.width(32)) adder_1 (.a(multiplexer_1_out), .b(PC_q), .out(adder_1_out));  // open: cin, cout
  // CND cnd_1: pin names not known; wires that end beside it: cc, ifun, cnd_1_p3
  // Probe on IMemReady
  // Probe on D_Data_from_RAM
  // Probe on in_18
  Adder #(.width(4)) adder_2 (.a(ifun), .b(icode), .out(adder_2_out));  // open: cin, cout
  Comparator #(.width(4)) comparator_1 (.a(icode), .b(4'b1101), .eq(comparator_1_eq));  // open: gt, lt
  Multiplexer #(.enable("false"), .width(32)) multiplexer_2 (
    .in0(adder_1_out), .in1(multiplexer_5_out), .out(multiplexer_2_out), .sel(cnd_1_p3));
  isplit isplit_1 (
    .Dest(isplit_1_dest), .D_V(isplit_1_d_v), .rA(rA), .rB(rB), .icode(icode), .ifun(ifun),
    .B1(ishim_1_out_7), .B2(ishim_1_out_8), .B3(ishim_1_out_9), .B4(ishim_1_out_10), .B5(ishim_1_out_11),
    .B0(ishim_1_out_6));
  ishim ishim_1 (
    .out_7(ishim_1_out_7), .out_8(ishim_1_out_8), .out_9(ishim_1_out_9), .out_10(ishim_1_out_10),
    .out_11(ishim_1_out_11), .out_6(ishim_1_out_6), .done(IMemReady), .RAMuse(I_RAMuse), .out_14(D_RAMAddr),
    .RAMread(I_RAMread), .in_2(PC_q), .reset(Reset), .req(IMemReq), .clock(out_25), .in_5(D_Data_from_RAM));
  // Probe on rB____F
  // Probe on in_7
  Multiplexer #(.enable("false"), .width(4)) multiplexer_3 (
    .in0(icode), .in1(adder_2_out), .out(multiplexer_3_out), .sel(comparator_1_eq));
  Multiplexer #(.enable("false"), .select(3), .width(32)) multiplexer_4 (
    .in0(dhsim_1_dataout), .in1(adder_1_out), .in2(multiplexer_5_out), .in3(multiplexer_2_out),
    .in4(32'h100), .in5(32'h200), .out(multiplexer_4_out), .sel({nextPCsel[2], in_23, in_24}));  // open: in6, in7
  // Probe on icode
  // Probe on ifun
  Multiplexer #(.enable("false"), .width(32)) multiplexer_5 (
    .in0(isplit_1_dest), .in1(isplit_1_d_v), .out(multiplexer_5_out), .sel(in_20));
  // Probe on multiplexer_5_out
  // Probe on {in_11, in_12}
  // Probe on multiplexer_4_out
  // Probe on rA
  // Probe on rB
  // Probe on in_15
  Multiplexer #(.enable("false"), .width(4)) multiplexer_6 (
    .in0(4'b0100), .in1(rB), .out(multiplexer_6_out), .sel(in_7));
  Multiplexer #(.enable("false"), .width(4)) multiplexer_7 (
    .in0(rA), .in1(4'b0100), .out(multiplexer_7_out), .sel(in_18));
  Multiplexer #(.enable("false"), .width(4)) multiplexer_8 (
    .in0(rB), .in1(4'b0100), .out(multiplexer_8_out), .sel(rB____F));
  // Probe on {in_9, in_10}
  FSM fsm_1 (
    .\output ({IMemReq, in_5, in_6, in_20, in_18, rB____F, in_7, in_11, in_12, in_15, in_9, in_10, in_17, _0_add, in_1, in_14, in_16, in_4, in_8, in_2, in_3, in_23, in_24, in_13, ldPriv, newPriv, nextPCsel[2], fsm_1_output}),
    .state(fsm_1_state), .DMemDone(DMemReady), .IMemDone(IMemReady), .reset(Reset), .clock(out_25),
    .icode(multiplexer_3_out), .exception(exception), .priv(priv));
  Bit_Extender #(.in_width(4), .out_width(3), .\type ("zero")) bit_extender_1 (
    .in(multiplexer_6_out), .out(bit_extender_1_out));
  Multiplexer #(.enable("false"), .select(2)) multiplexer_9 (
    .in0(1'b0), .in1(1'b1), .in2(cnd_1_p3), .out(multiplexer_9_out), .sel({in_11, in_12}));  // open: in3
  Bit_Extender #(.in_width(4), .out_width(3), .\type ("zero")) bit_extender_2 (.in(rA), .out(bit_extender_2_out));
  Bit_Extender #(.in_width(4), .out_width(3), .\type ("zero")) bit_extender_3 (
    .in(multiplexer_7_out), .out(bit_extender_3_out));
  Bit_Extender #(.in_width(4), .out_width(3), .\type ("zero")) bit_extender_4 (
    .in(multiplexer_8_out), .out(bit_extender_4_out));
  Comparator #(.width(4)) comparator_2 (.a(multiplexer_8_out), .b(4'b1111), .eq(comparator_2_eq));  // open: gt, lt
  // Probe on in_17
  // Probe on fsm_1_state
  regwriter regwriter_1 (
    .D4(regwriter_1_d4), .EN_5(regwriter_1_en_5), .D5(regwriter_1_d5), .D0(regwriter_1_d0),
    .EN_6(regwriter_1_en_6), .D6(regwriter_1_d6), .EN_7(regwriter_1_en_7), .D7(regwriter_1_d7),
    .EN(regwriter_1_en), .EN_8(regwriter_1_en_8), .D1(regwriter_1_d1), .EN_2(regwriter_1_en_2),
    .D2(regwriter_1_d2), .EN_3(regwriter_1_en_3), .D3(regwriter_1_d3), .EN_4(regwriter_1_en_4),
    .reqE(multiplexer_9_out), .reqM(in_15), .dstE(bit_extender_1_out), .dstM(bit_extender_2_out),
    .valE(alu_1_vale___alub_op_alua), .valM(dhsim_1_dataout));
  Register #(.width(32)) eax (.D(regwriter_1_d0), .en(regwriter_1_en), .Q(eax_q), .clk(out_25), .clr(regreader_1_clr));
  Register #(.width(32)) ecx (
    .D(regwriter_1_d1), .en(regwriter_1_en_2), .Q(ecx_q), .clk(out_25), .clr(regreader_1_clr_2));
  Register #(.width(32)) edx (
    .D(regwriter_1_d2), .en(regwriter_1_en_3), .Q(edx_q), .clk(out_25), .clr(regreader_1_clr_3));
  Register #(.width(32)) ebx (
    .D(regwriter_1_d3), .en(regwriter_1_en_4), .Q(ebx_q), .clk(out_25), .clr(regreader_1_clr_4));
  Register #(.width(32)) esp (
    .D(regwriter_1_d4), .en(regwriter_1_en_5), .Q(esp_q), .clk(out_25), .clr(regreader_1_clr_5));
  Register #(.width(32)) ebp (
    .D(regwriter_1_d5), .en(regwriter_1_en_6), .Q(ebp_q), .clk(out_25), .clr(regreader_1_clr_6));
  Register #(.width(32)) esi (
    .D(regwriter_1_d6), .en(regwriter_1_en_7), .Q(esi_q), .clk(out_25), .clr(regreader_1_clr_7));
  Register #(.width(32)) edi (
    .D(regwriter_1_d7), .en(regwriter_1_en_8), .Q(edi_q), .clk(out_25), .clr(regreader_1_clr_8));
  // Probe on _0_add
  regreader regreader_1 (
    .valA(regreader_1_vala), .valB(regreader_1_valb), .CLR_5(regreader_1_clr_5), .CLR_6(regreader_1_clr_6),
    .CLR_7(regreader_1_clr_7), .CLR_8(regreader_1_clr_8), .CLR(regreader_1_clr), .CLR_2(regreader_1_clr_2),
    .CLR_3(regreader_1_clr_3), .CLR_4(regreader_1_clr_4), .reset(Reset), .srcA(bit_extender_3_out),
    .srcB(bit_extender_4_out), .Q_5(esp_q), .Q_6(ebp_q), .Q_7(esi_q), .Q_8(edi_q), .Q(eax_q), .Q_2(ecx_q),
    .Q_3(edx_q), .Q_4(ebx_q));
  // Probe on in_1
  // Probe on regreader_1_vala
  // Probe on regreader_1_valb
  // Probe on multiplexer_5_out
  // Probe on in_16
  // Probe on in_14
  Comparator #(.mode("unsigned"), .width(4)) comparator_3 (.a(rA), .b(4'b0111), .gt(comparator_3_gt));  // open: eq, lt
  Comparator #(.width(4)) comparator_4 (.a(rA), .b(4'b1111), .eq(comparator_4_eq));  // open: gt, lt
  Comparator #(.mode("unsigned"), .width(4)) comparator_5 (.a(rB), .b(4'b0111), .gt(comparator_5_gt));  // open: eq, lt
  Comparator #(.width(4)) comparator_6 (.a(rB), .b(4'b1111), .eq(comparator_6_eq), .lt(comparator_6_lt));  // open: gt
  Multiplexer #(.enable("false"), .select(2), .width(32)) multiplexer_10 (
    .in0(regreader_1_vala), .in1(multiplexer_5_out), .in2(32'hfffffffc), .in3(32'h4),
    .out(multiplexer_10_out), .sel({in_9, in_10}));
  Multiplexer #(.enable("false"), .width(32)) multiplexer_11 (
    .in0({32{1'b0}}), .in1(regreader_1_valb), .out(multiplexer_11_out), .sel(and_1_out));
  and and_1 (and_1_out, ~comparator_2_eq, in_17);  // AND_Gate
  Multiplexer #(.enable("false"), .width(4)) multiplexer_12 (
    .in0(4'b0000), .in1(ifun), .out(multiplexer_12_out), .sel(_0_add));
  // Probe on in_4
  Register #(.width(1)) register_1 (.D(newPriv), .en(ldPriv), .Q(priv), .clk(out_25), .clr(Reset));
  and and_2 (and_2_out, comparator_5_gt, comparator_6_lt);
  alu alu_1 (
    .aluA(multiplexer_10_out), .aluB(multiplexer_11_out), .aluOP(multiplexer_12_out),
    .valE___aluB_OP_aluA(alu_1_vale___alub_op_alua), .CC(alu_1_cc));
  // Probe on in_8
  // Probe on in_2
  or or_1 (or_1_out, comparator_3_gt, comparator_5_gt);
  or or_2 (or_2_out, ~comparator_4_eq, comparator_5_gt);  // OR_Gate
  or or_3 (or_3_out, comparator_3_gt, ~comparator_6_eq);  // OR_Gate
  or or_4 (or_4_out, comparator_3_gt, and_2_out);
  // Probe on cc
  Register #(.width(3)) u_CC (.D(alu_1_cc), .en(in_1), .Q(cc), .clk(out_25), .clr(Reset));
  // Probe on in_3
  Multiplexer #(.enable("false"), .select(4)) multiplexer_13 (
    .in0(1'b0), .in1(1'b0), .in2(or_1_out), .in3(or_2_out), .in4(or_4_out), .in5(or_4_out), .in6(or_1_out),
    .in7(1'b0), .in8(1'b0), .in9(1'b0), .in10(or_3_out), .in11(or_3_out), .in12(or_1_out), .in13(1'b0),
    .in14(1'b0), .in15(1'b0), .out(multiplexer_13_out), .sel(icode));
  // Probe on adder_1_out
  // Probe on alu_1_vale___alub_op_alua
  Multiplexer #(.enable("false"), .width(32)) multiplexer_14 (
    .in0(adder_1_out), .in1(regreader_1_vala), .out(multiplexer_14_out), .sel(in_4));
  Multiplexer #(.enable("false"), .width(32)) multiplexer_15 (
    .in0(alu_1_vale___alub_op_alua), .in1(regreader_1_vala), .out(multiplexer_15_out), .sel(in_14));
  // Probe on {in_23, in_24}
  and and_3 (exception, multiplexer_13_out, IMemReady);
  Register #(.width(32)) MDR (.D(multiplexer_14_out), .en(in_8), .Q(MDR_q), .clk(out_25), .clr(Reset));
  Register #(.width(32)) MAR (.D(multiplexer_15_out), .en(in_16), .Q(MAR_q), .clk(out_25), .clr(Reset));
  // Probe on in_13
  LED led_1 (.in(exception));
  Button button_1 ();  // open: out
  // Probe on D_RAMuse
  // Probe on D_RAMAddr
  // Probe on ldPriv
  // Probe on dhsim_1_dataout
  // Probe on D_RAMread
  // Probe on D_RAMWrite
  // Probe on D_Data_to_RAM
  // Probe on newPriv
  dhsim dhsim_1 (
    .out_9(D_Data_to_RAM), .RAMwrite(D_RAMWrite), .RAMread(D_RAMread), .done(DMemReady),
    .DataOut(dhsim_1_dataout), .RAMuse(D_RAMuse), .out_14(D_RAMAddr), .in_2(D_Data_from_RAM), .in_1(MAR_q),
    .DMem_Write(in_3), .req(in_2), .reset(Reset), .clock(out_25), .in_3(MDR_q));
  // Probe on D_Data_from_RAM
  // Probe on dhsim_1_dataout
  // Probe on DMemReady
  or or_5 (or_5_out, D_RAMuse, I_RAMuse);
  or or_6 (or_6_out, D_RAMread, I_RAMread);
  assign controlled_buffer_1_out = kbyte_buddy_1_sel ? kbyte_buddy_1_ram_addr : 10'bz;  // Controlled_Buffer controlled_buffer_1
  kbyte_buddy kbyte_buddy_1 (
    .ram_addr(kbyte_buddy_1_ram_addr), .sel(kbyte_buddy_1_sel), .addr(D_RAMAddr), .addr_prefix({32{1'b0}}),
    .\use (or_5_out));
  assign controlled_buffer_2_out = kbyte_buddy_2_sel ? kbyte_buddy_2_ram_addr : 10'bz;  // Controlled_Buffer controlled_buffer_2
  kbyte_buddy kbyte_buddy_2 (
    .ram_addr(kbyte_buddy_2_ram_addr), .sel(kbyte_buddy_2_sel), .addr(D_RAMAddr), .addr_prefix(32'h400),
    .\use (or_5_out));
  and and_4 (and_4_out, or_5_out, ~priv);  // AND_Gate
  ROM #(.addrWidth(10)) rom_1 (.addr(controlled_buffer_1_out), .data(D_Data_from_RAM));
  // Probe on controlled_buffer_1_out
  RAM #(.addrWidth(10)) ram_1 (
    .addr(controlled_buffer_2_out), .we(D_RAMWrite), .clk(out_25), .din(D_Data_to_RAM), .dout(D_Data_from_RAM));
  // Probe on controlled_buffer_2_out
  io io_1 (
    .KB_Status(keyboard_1_avail), .KB_Data(keyboard_1_data), .KB_read_enable(io_1_kb_read_enable),
    .RAM_Use(and_4_out), .KB_Clear(io_1_kb_clear), .Outgoing_Data(D_Data_from_RAM), .in_4(D_RAMAddr),
    .in_5(D_Data_to_RAM), .RAM_Read(or_6_out), .RAM_Write(D_RAMWrite), .TTY_Ready(1'b1),
    .TTY_Data(io_1_tty_data), .TTY_Enable(io_1_tty_enable), .reset(Reset), .TTY_Clear(io_1_tty_clear));
  Keyboard keyboard_1 (
    .clk(out_25), .re(io_1_kb_read_enable), .clr(io_1_kb_clear), .avail(keyboard_1_avail),
    .data(keyboard_1_data));
  TTY tty_1 (.data(io_1_tty_data), .clk(out_25), .we(io_1_tty_enable), .clr(io_1_tty_clear));

  // Other names for the same wires on the sheet: ldPC = in_13; DMemWrite = in_3; DMemReq = in_2; ldMDR = in_8;
  //   MDRsel = in_4; ldMAR = in_16; MARsel = in_14; ldCC = in_1; aluOPsel = _0_add; aluBsel = in_17;
  //   aluAsel[1:0] = {in_9, in_10}; dstMreq = in_15; dstEreq[1:0] = {in_11, in_12}; dstEsel = in_7; srcBsel = rB____F;
  //   srcAsel = in_18; valCsel = in_20; PCIncSel[1:0] = {in_5, in_6}; Clock = out_25;
  //   I_Data_from_RAM[7:0] = D_Data_from_RAM; I_RAMAddr[31:0] = D_RAMAddr; newPCsel[1:0] = {in_23, in_24};
  //   nextPCsel[1:0] = {in_23, in_24}; sysPCsel = nextPCsel[2]

  // Notes on the sheet:
  //   Y86 Skeleton
  //   Oct 2024
  //   connect to memory!
  //   Fetch
  //   icode == d ? icode + ifun : icode 
  //   valP
  //   when the machine first starts running, privmode = 0 and PC = 0 
  //   valM
  //   IR[1:4]
  //   IR[2:5]
  //   Decode/Write-Back
  //   0-3: normal operations
  //   4: sysenter (newPCsel = 00)
  //   5: exception && priv == 1
  //   SWS and Taylor Cathcart and Vijay Kothari, based on a skeleton from Matt Kretchmar
  //   Execute
  //   Memory
  //   0: privileged/kernel mode
  //   1: unprivileged/user mode
  //   PC
  //   Assumes ISHIM and DSHIM won't assert RAMuse simultaneously
  //   (so D RAMAddr, I RAMAddr won't both be non-floating at the 
  //   same time)
  //   privmode must be zero for any I/O operations
  //   illegal register exceptions (by icode):
  //   00: N/A
  //   10: N/A
  //   2X: rA > 7 or rB > 7
  //   30: rA != F or rB > 7
  //   40: rA > 7 or 7 < rB < F
  //   50: rA > 7 or 7 < rB < F
  //   6X: rA > 7 or rB > 7
  //   7X: N/A
  //   80: N/A
  //   90: N/A
  //   A0: rA > 7 or rB != F
  //   B0: rA > 7 or rB != F
  //   C0: rA > 7 or rB > 7
  //   D0: N/A
  //   E0: N/A
  //   F0: N/A
  //   Privilege
  //   connect to memory (and io,
  //    pretending to be memory)
  //   Privilege/Exception
  //   contents of rom_1 (hex, n*v repeats v):
  //   30 f4 0 5 0 0 30 f2 c 2 0 0 80 d 1 0 0 d0 70 0 3 235*0 30 f2 11 2 0 0 80 d 1 0 0 d0 90 30 f6 4*0 30
  //   f7 1 0 0 0 30 f3 ff 0 0 0 50 2 4*0 62 30 73 38 1 0 0 80 39 1 0 0 60 72 70 1f 1 0 0 90 50 1f 8 fe ff
  //   0 60 61 73 39 1 0 0 40 f c fe ff 0 90 179*0 30 f2 17 2 0 0 80 d 1 0 0 0 48 69 21 20 0 59 65 73 3f 20
  //   0 55 68 2d 6f 68 21 20 226*0 10 d1 10 10 20 88 10
  //   a kilobyte of ROM living at 0x00000000, for code
  //   a kilobyte of RAM, living somewhere else, for data
endmodule

module isplit (
  input  [7:0] B0,
  input  [7:0] B1,
  input  [7:0] B2,
  input  [7:0] B3,
  input  [7:0] B4,
  input  [7:0] B5,
  output [3:0] icode,
  output [3:0] ifun,
  output [3:0] rA,
  output [3:0] rB,
  output [31:0] Dest,
  output [31:0] D_V
);


  assign D_V = {B5, B4, B3, B2};
  assign Dest = {B4, B3, B2, B1};
  assign icode = B0[7:4];
  assign ifun = B0[3:0];
  assign rA = B1[7:4];
  assign rB = B1[3:0];
endmodule

module MSB (
  input  [31:0] Value,
  output MSB
);


  assign MSB = Value[31];
endmodule

module ishim (
  input  req,
  input  [31:0] in_2,
  input  reset,
  input  clock,
  input  [7:0] in_5,
  output [7:0] out_6,
  output [7:0] out_7,
  output [7:0] out_8,
  output [7:0] out_9,
  output [7:0] out_10,
  output [7:0] out_11,
  output done,
  output RAMuse,
  output [31:0] out_14,
  output RAMread
);

  wire decoder_1_out0, decoder_1_out1, decoder_1_out2, decoder_1_out3, decoder_1_out4, decoder_1_out5,
       decoder_1_out6, or_1_out;
  wire [2:0] _3bit_q;
  wire [31:0] adder_1_out, bit_extender_1_out;

  D_Flip_Flop #(.enable("true")) d_ff_1 (
    .clk(clock), .D(req), .Q(RAMread), .Qn(done), .preset(1'b0), .en(done), .reset(or_1_out));
  Decoder #(.select(3)) decoder_1 (
    .out0(decoder_1_out0), .out1(decoder_1_out1), .out2(decoder_1_out2), .out3(decoder_1_out3),
    .out4(decoder_1_out4), .out5(decoder_1_out5), .out6(decoder_1_out6), .sel(_3bit_q), .en(RAMread));  // open: out7
  Counter #(.max('h7), .width(3)) _3bit (
    .load(1'b0), .count(RAMread), .Q(_3bit_q), .clk(clock), .clr(or_1_out));  // open: D, carry
  or or_1 (or_1_out, decoder_1_out6, reset);
  assign bit_extender_1_out = {{29{1'b0}}, _3bit_q};  // Bit_Extender bit_extender_1
  Adder #(.width(32)) adder_1 (.a(in_2), .b(bit_extender_1_out), .out(adder_1_out), .cin(1'b0));  // open: cout
  assign out_14 = RAMread ? adder_1_out : 32'bz;  // Controlled_Buffer controlled_buffer_1
  Register #(.trigger("falling")) register_1 (.D(in_5), .en(decoder_1_out0), .Q(out_6), .clk(clock), .clr(reset));
  Register #(.trigger("falling")) register_2 (.D(in_5), .en(decoder_1_out1), .Q(out_7), .clk(clock), .clr(reset));
  Register #(.trigger("falling")) register_3 (.D(in_5), .en(decoder_1_out2), .Q(out_8), .clk(clock), .clr(reset));
  Register #(.trigger("falling")) register_4 (.D(in_5), .en(decoder_1_out3), .Q(out_9), .clk(clock), .clr(reset));
  Register #(.trigger("falling")) register_5 (.D(in_5), .en(decoder_1_out4), .Q(out_10), .clk(clock), .clr(reset));
  Register #(.trigger("falling")) register_6 (.D(in_5), .en(decoder_1_out5), .Q(out_11), .clk(clock), .clr(reset));

  assign RAMuse = RAMread;

  // Notes on the sheet:
  //   addr
  //   in use?
  //   state
  //   RAMaddr (32 bits)
  //   data from RAM (8 bits)
  //   byte 0
  //   byte 1
  //   byte 2
  //   byte 3
  //   byte 4
  //   byte 5
endmodule

module dhsim (
  input  [31:0] in_1,
  input  [7:0] in_2,
  input  [31:0] in_3,
  input  DMem_Write,
  input  req,
  input  reset,
  input  clock,
  output [31:0] DataOut,
  output [7:0] out_9,
  output RAMwrite,
  output RAMread,
  output done,
  output RAMuse,
  output [31:0] out_14
);

  wire comparator_1_eq, d_ff_1_q, d_ff_1_qn, decoder_1_out0, decoder_1_out1, decoder_1_out2, decoder_1_out3,
       or_1_out;
  wire [1:0] bit_extender_2_out;
  wire [2:0] _3bit_q;
  wire [31:0] adder_1_out, bit_extender_1_out;

  assign bit_extender_1_out = {{29{1'b0}}, _3bit_q};  // Bit_Extender bit_extender_1
  D_Flip_Flop #(.enable("true")) d_ff_1 (
    .clk(clock), .D(DMem_Write), .Q(d_ff_1_q), .Qn(d_ff_1_qn), .preset(1'b0), .en(done), .reset(reset));
  D_Flip_Flop #(.enable("true")) in_use (
    .clk(clock), .D(req), .Q(RAMuse), .Qn(done), .preset(1'b0), .en(done), .reset(or_1_out));
  Adder #(.width(32)) adder_1 (.a(in_1), .b(bit_extender_1_out), .out(adder_1_out), .cin(1'b0));  // open: cout
  and and_1 (RAMwrite, RAMuse, d_ff_1_q);
  and and_2 (RAMread, d_ff_1_qn, RAMuse);
  Decoder #(.select(3)) decoder_1 (
    .out0(decoder_1_out0), .out1(decoder_1_out1), .out2(decoder_1_out2), .out3(decoder_1_out3),
    .sel(_3bit_q), .en(RAMread));  // open: out4, out5, out6, out7
  Counter #(.max('h7), .width(3)) _3bit (
    .load(1'b0), .count(RAMuse), .Q(_3bit_q), .clk(clock), .clr(or_1_out));  // open: D, carry
  or or_1 (or_1_out, comparator_1_eq, reset);
  Comparator #(.mode("unsigned"), .width(3)) comparator_1 (
    .a(_3bit_q), .b(3'b100), .eq(comparator_1_eq));  // open: gt, lt
  assign out_14 = RAMuse ? adder_1_out : 32'bz;  // Controlled_Buffer controlled_buffer_1
  Bit_Extender #(.in_width(3), .out_width(2)) bit_extender_2 (.in(_3bit_q), .out(bit_extender_2_out));
  Multiplexer #(.select(2), .width(8)) multiplexer_1 (
    .in0(in_3[7:0]), .in1(in_3[15:8]), .in2(in_3[23:16]), .in3(in_3[31:24]), .out(out_9),
    .sel(bit_extender_2_out), .en(RAMwrite));
  Register #(.trigger("falling")) register_1 (
    .D(in_2), .en(decoder_1_out0), .Q(DataOut[7:0]), .clk(clock), .clr(reset));
  Register #(.trigger("falling")) register_2 (
    .D(in_2), .en(decoder_1_out1), .Q(DataOut[15:8]), .clk(clock), .clr(reset));
  Register #(.trigger("falling")) register_3 (
    .D(in_2), .en(decoder_1_out2), .Q(DataOut[23:16]), .clk(clock), .clr(reset));
  Register #(.trigger("falling")) register_4 (
    .D(in_2), .en(decoder_1_out3), .Q(DataOut[31:24]), .clk(clock), .clr(reset));

  // Notes on the sheet:
  //   address
  //   writing?
  //   reading?
  //   state
  //   data in
  //   RAMaddr (32 bits)
  //   data from RAM (8 bits)
  //   data to RAM (8 bits)
endmodule

module kbyte_buddy (
  input  [31:0] addr,
  input  [31:0] addr_prefix,
  input  \use ,
  output [9:0] ram_addr,
  output sel
);

  wire comparator_1_eq;
  wire [31:0] and_1_out;

  Bit_Extender #(.in_width(32), .out_width(10), .\type ("zero")) bit_extender_1 (.in(addr), .out(ram_addr));
  // Probe on and_1_out
  assign and_1_out = addr & 32'hfffffc00;  // AND_Gate and_1, 32 bits wide
  Comparator #(.mode("unsigned"), .width(32)) comparator_1 (
    .a(and_1_out), .b(addr_prefix), .eq(comparator_1_eq));  // open: gt, lt
  and and_2 (sel, comparator_1_eq, \use );
endmodule

module FSM (
  input  exception,
  input  priv,
  input  [3:0] icode,
  input  reset,
  input  DMemDone,
  input  clock,
  input  IMemDone,
  output [5:0] state,
  output [31:0] \output 
);

  wire and_1_out, d_ff_1_q;
  wire [1:0] s;
  wire [3:0] rom_2_data;
  wire [5:0] multiplexer_2_out, register_1_q, useq_1_nextstate, valN;

  D_Flip_Flop d_ff_1 (.clk(clock), .D(exception), .Q(d_ff_1_q), .reset(reset));  // open: Qn, preset
  Multiplexer #(.enable("false"), .width(6)) multiplexer_1 (
    .in0(useq_1_nextstate), .in1(multiplexer_2_out), .out(state), .sel(and_1_out));
  and and_1 (and_1_out, exception, ~d_ff_1_q);  // AND_Gate
  Multiplexer #(.enable("false"), .width(6)) multiplexer_2 (
    .in0(6'b110000), .in1(6'b001010), .out(multiplexer_2_out), .sel(priv));
  // Probe on state
  // Probe on register_1_q
  Register #(.width(6)) register_1 (.D(state), .Q(register_1_q), .clk(clock), .clr(reset));  // open: en
  ROM #(.addrWidth(6), .dataWidth(32)) rom_1 (.addr(register_1_q), .data(\output ));
  ROM #(.addrWidth(6), .dataWidth(12)) rom_2 (.addr(register_1_q), .data({s, valN, rom_2_data}));
  // Probe on \output 
  // Probe on {s, valN, rom_2_data}
  useq useq_1 (
    .CurrentState(register_1_q), .valN(valN), .icode(icode), .DMemReady(DMemDone), .IMemReady(IMemDone),
    .select(s), .NextState(useq_1_nextstate));

  // Notes on the sheet:
  //   send special state only on the
  //    rising edge of "exception"
  //   if exception and priv == 0, halt
  //   if exception and priv == 1, exc 
  //   microinstructions
  //   contents of rom_1 (hex, n*v repeats v):
  //   80000000 0 1800 0 1000 0 400000 1000 0 100 3a0 38*0 60000300 43000300 12900300 1018e300 10188300
  //   428e0300 20000700 24a8a500 cb98000 44a8e300 4cb98300 129e0300 600003c0 64a8a1a0
  //   for microsequencer
  //   contents of rom_2 (hex, n*v repeats v):
  //   410 c00 430 800 450 860 400 480 890 400 400 38*0 400 400 400 420 440 400 400 420 470 420 440 400 400
  //   420
  //   microinstruction
endmodule
